# Fritzing sketch premiere-breadboard (saved by Fritzing 0.9.5d)
breadboards: 1

parts:
  T1 = LM35 Temperature Sensor [package="TO92 [THT]"]
  Adafruit_HUZZAH_ESP8266_Breakout1 = Adafruit HUZZAH ESP8266 Breakout [part_number=2471]
  LED1 = smd LED [color="Red (633nm)" package="0603 [SMD]"]
  R1 = Resistor [tolerance=±5% resistance=220 package="0402 [SMD]"]
  R2 = Resistor [tolerance=±5% resistance=220 package="0402 [SMD]"]
  Q1 = PNP-Transistor [package="TO92 [THT]"]

nets:
  N1: T1.+Vs, Q1.E
  N2: T1.Vout, R2.Pin_1
  GND: T1.GND, Adafruit_HUZZAH_ESP8266_Breakout1.GND, LED1.cathode
  N3: Adafruit_HUZZAH_ESP8266_Breakout1.#16, R1.Pin_1
  N4: Adafruit_HUZZAH_ESP8266_Breakout1.A, R2.Pin_0
  N5: Adafruit_HUZZAH_ESP8266_Breakout1.#4, Q1.C
  N6: Adafruit_HUZZAH_ESP8266_Breakout1.3V, Q1.B
  N7: LED1.anode, R1.Pin_0
